# Fritzing sketch Olbin (saved by Fritzing 0.9.3b)

parts:
  부품1 = Arduino Uno (Rev3)
  부품2 = Matrix LED de 8x8 basada en MAX7219
  HC-SR04_Sensor_1 = HC-SR04 Ultrasonic Distance Sensor
  U1 = SWITCH_SPDT [package=kps-1290]
  BAT1 = 18650 battery holder [package=battery-18650-kit]
  U3 = Mini-360 DC-DC Buck converter [package=THT]
  U4 = Mini-360 DC-DC Buck converter [package=THT]
  H1 = polarizedheader 4pin 0.156in [package=THT]
  M1 = Dagu DGServo 9g (Top view) [part_number=RS001B]
  S1 = Momentary Switch [package=ksa_sealed_tac_switch]
  R1 = Resistor [tolerance=±5% resistance=220 package=THT]
  TP1 = TP4056 [chip_label=TP4056 package="DIP (Dual Inline) [THT]"]

nets:
  N1: 부품1.D9_PWM, M1.pulse
  N2: 부품1.D11_PWM/MOSI, 부품2.DIN
  N3: 부품1.D12/MISO, 부품2.CS
  N4: 부품1.D13/SCK, 부품2.CLK
  N5: 부품1.D2, S1.1
  N6: 부품1.D4, H1.pin1
  N7: 부품1.D5_PWM, H1.pin2
  N8: 부품1.D6_PWM, HC-SR04_Sensor_1.ECHO
  N9: 부품1.D7, HC-SR04_Sensor_1.TRIG
  GND: 부품1.GND, 부품2.GND, HC-SR04_Sensor_1.GND, U3.OUT-, U4.OUT-, M1.gnd, R1.Pin_0
  N10: 부품1.VIN, U3.OUT+
  VCC: 부품2.VCC, HC-SR04_Sensor_1.VCC, U4.OUT+, M1.vcc, S1.2
  N11: U1.O, TP1.pin3
  N12: U1.S, U3.IN+, U4.IN+
  N13: BAT1.+, TP1.pin4
  N14: BAT1.-, TP1.pin5
  N15: U3.IN-, U4.IN-, TP1.pin6
  N16: S1.4, R1.Pin_1

notes:
  CM-50 Serial
  7V Step up
  5V Step up
  CM-50 Power

custom parts:
  18650 battery holder: 18650 Battery Holder
  Mini-360 DC-DC Buck converter: Mini-360 DC-DC Buck converter. Tiny buck step down voltage converter, input voltage 4.75 to 23V output 1 to 17V adjustable. Available from ebay and the like.
  TP4056: A DIP stand-in part for whatever IC you want. With 6 pins on a 300mil dual inline package (DIP) footprint.
